// Logisim project cpu_design.circ as structural Verilog: 5 circuits, main circuit main
module main (
  input  [7:0] input_a,
  input  [7:0] input_b,
  input  enable,
  input  clear
);

  wire clock_out;

  Register register_1 (.D(input_b), .en(enable), .Q(input_a), .clk(clock_out), .clr(clear));
  Clock clock (.out(clock_out));

  // Notes on the sheet:
  //   register a
endmodule

// au
module AU (
  input  [7:0] input_b,
  input  [7:0] input_a,
  input  mode_sub_add,
  output C_OUT,
  output [7:0] \output ,
  output z_flag,
  output overflow_flag
);

  wire xnor_1_out, xor_2_out;
  wire [7:0] bit_extender_1_out, xor_1_out;

  assign bit_extender_1_out = {{7{mode_sub_add}}, mode_sub_add};  // Bit_Extender bit_extender_1
  assign xor_1_out = input_b ^ bit_extender_1_out;  // XOR_Gate xor_1, 8 bits wide
  xor xor_2 (xor_2_out, \output [7], input_b[7]);
  xnor xnor_1 (xnor_1_out, input_b[7], input_a[7]);
  Adder adder_1 (.a(input_a), .b(xor_1_out), .out(\output ), .cin(mode_sub_add), .cout(C_OUT));
  and and_1 (overflow_flag, xor_2_out, xnor_1_out);
  Comparator comparator_1 (.a(\output ), .b({8{1'b0}}), .eq(z_flag));  // open: gt, lt
endmodule

module LU (
  input  [7:0] input_a,
  input  [7:0] input_b,
  input  _1,
  input  _2,
  output [7:0] \output 
);

  wire [7:0] and_1_out, not_1_out, or_1_out, xor_1_out;

  assign xor_1_out = input_a ^ input_b;  // XOR_Gate xor_1, 8 bits wide
  assign or_1_out = input_a | input_b;  // OR_Gate or_1, 8 bits wide
  assign and_1_out = input_a & input_b;  // AND_Gate and_1, 8 bits wide
  assign not_1_out = ~input_a;  // NOT_Gate not_1, 8 bits wide
  Multiplexer #(.select(2), .width(8), .enable("false")) multiplexer_1 (
    .in0(xor_1_out), .in1(or_1_out), .in2(and_1_out), .in3(not_1_out), .out(\output ), .sel({_1, _2}));
endmodule

module ALU_Final (
  input  [3:0] Opcode,
  input  [7:0] input_a,
  input  [7:0] input_b,
  output carry_out,
  output [7:0] out_5,
  output z_flag,
  output overflow_flag
);

  wire [7:0] arthmetic_unit_output, logic_unit_output, multiplexer_1_out, multiplexer_2_out, not_1_out,
       not_2_out;

  assign not_1_out = ~input_a;  // NOT_Gate not_1, 8 bits wide
  assign not_2_out = ~input_b;  // NOT_Gate not_2, 8 bits wide
  Multiplexer #(.width(8)) multiplexer_1 (
    .in0(input_a), .in1(not_1_out), .out(multiplexer_1_out), .sel(Opcode[0]));  // open: en
  Multiplexer #(.width(8)) multiplexer_2 (
    .in0(input_b), .in1(not_2_out), .out(multiplexer_2_out), .sel(Opcode[1]));  // open: en
  AU arthmetic_unit (
    .input_b(multiplexer_2_out), .input_a(multiplexer_1_out), .mode_sub_add(Opcode[2]), .C_OUT(carry_out),
    .\output (arthmetic_unit_output), .z_flag(z_flag), .overflow_flag(overflow_flag));
  LU logic_unit (
    .input_a(input_a), .input_b(multiplexer_2_out), ._1(Opcode[2]), ._2(Opcode[0]),
    .\output (logic_unit_output));
  Multiplexer #(.width(8)) multiplexer_3 (
    .in0(arthmetic_unit_output), .in1(logic_unit_output), .out(out_5), .sel(Opcode[3]));  // open: en

  // Other names for the same wires on the sheet: f0 = Opcode[0]; f1 = Opcode[1]; f2 = Opcode[2]; f3 = Opcode[3]
endmodule

module Register_File (
  input  [7:0] Data_in,
  input  write_enable,
  input  [1:0] read_addr_a,
  input  [1:0] write_addr,
  input  [1:0] read_addr_b,
  input  reset,
  output [7:0] Value_a,
  output [7:0] value_b
);

  wire clock_out, demultiplexer_1_out0, demultiplexer_1_out1, demultiplexer_1_out2, demultiplexer_1_out3;
  wire [3:0] register_1_q, register_1_q_2;
  wire [7:0] register_2_q, register_3_q, register_4_q;

  Demultiplexer #(.select(2)) demultiplexer_1 (
    .out0(demultiplexer_1_out0), .out1(demultiplexer_1_out1), .out2(demultiplexer_1_out2),
    .out3(demultiplexer_1_out3), .in(write_enable), .sel(write_addr));  // open: en
  Clock clock (.out(clock_out));
  Hex_Digit_Display hex_digit_display_1 (.value(register_1_q_2));  // open: dp
  Register register_1 (
    .D(Data_in), .en(demultiplexer_1_out0), .Q({register_1_q_2, register_1_q}), .clk(clock_out), .clr(reset));
  Register register_2 (.D(Data_in), .en(demultiplexer_1_out1), .Q(register_2_q), .clk(clock_out), .clr(reset));
  Register register_3 (.D(Data_in), .en(demultiplexer_1_out2), .Q(register_3_q), .clk(clock_out), .clr(reset));
  Register register_4 (.D(Data_in), .en(demultiplexer_1_out3), .Q(register_4_q), .clk(clock_out), .clr(reset));
  Hex_Digit_Display hex_digit_display_2 (.value(register_1_q));  // open: dp
  Multiplexer #(.select(2), .width(8)) multiplexer_1 (
    .in0({register_1_q_2, register_1_q}), .in1(register_2_q), .in2(register_3_q), .in3(register_4_q),
    .out(Value_a), .sel(read_addr_a));  // open: en
  Multiplexer #(.select(2), .width(8)) multiplexer_2 (
    .in0({register_1_q_2, register_1_q}), .in1(register_2_q), .in2(register_3_q), .in3(register_4_q),
    .out(value_b), .sel(read_addr_b));  // open: en

  // Notes on the sheet:
  //   rs1
  //   rs2
  //   rs3
  //   rs4
endmodule
